# Fritzing sketch Sensor Project (saved by Fritzing 0.9.3b)
circuit board: 13.7724cm x 6.858cm
breadboards: 1

parts:
  U1 = NodeMCU V1.0
  R1 = Resistor [tolerance=±5% resistance=4.7k package="0603 [SMD]"]
  GY1 = MPU-6050 Board GY-521 [form="♀ (female)" package=THT]
  Squix1 = OLED 0.96" 128x64 I2C SSD1306
  S1 = Pushbutton [package="[THT]"]
  TRS2 = Audio Jack (TRS) 3.5mm [package="4Ucon 08780 [THT]"]
  TRS1 = Audio Jack (TRS) 3.5mm [package="4Ucon 08780 [THT]"]
  TRS3 = Audio Jack (TRS) 3.5mm [package="4Ucon 08780 [THT]"]
  Part1 = Humidity Temperature Sensor SI7021  # not connected

nets:
  N1: U1.D1, GY1.pin3
  N2: U1.D2, GY1.pin4, Squix1.SCA
  N3: U1.3V3, R1.Pin_1, S1.Pin_3, S1.Pin_4, TRS2.Tip, TRS1.Tip, TRS3.Tip
  N4: U1.GND, TRS2.Sleeve, TRS1.Sleeve
  N5: U1.D5, S1.Pin_1, S1.Pin_2
  N6: U1.D6, R1.Pin_0, TRS2.Ring, TRS1.Ring
  N7: U1.A0, TRS3.Ring
  N8: GY1.pin1, Squix1.GND

custom parts:
  NodeMCU V1.0: ESP9266 based NodeMCU
  MPU-6050 Board GY-521: Acelerometro y Giroscopio MPU-6050 Board GY-521
  Humidity Temperature Sensor SI7021: SI7021 sensor breakout board.
